// Logisim project JAV_RISCV (1).circ as structural Verilog: 8 circuits, main circuit main
module main (
  input  RESET,
  input  in_2,
  input  in_3
);

  wire alu_1_out_5, clock_1_out, control_unit_1_out_3, control_unit_1_out_4, control_unit_1_out_5,
       control_unit_1_out_6, control_unit_1_out_7, control_unit_1_out_8, control_unit_1_out_9,
       control_unit_1_out_11, control_unit_1_out_12, control_unit_1_out_13, undriven_2, undriven_3;
  wire [1:0] control_unit_1_out_10;
  wire [4:0] aluop_1_out_4, multiplexer_5_out, undriven;
  wire [23:0] register_1_q_2;
  wire [31:0] adder_1_out, alu_1_out_4, immediate_generator_1_out_3, immediate_generator_1_out_4,
       immediate_generator_1_out_5, immediate_generator_1_out_6, immediate_generator_1_out_7,
       multiplexer_1_out, multiplexer_2_out, multiplexer_3_out, multiplexer_4_out, multiplexer_6_out,
       multiplexer_7_out, multiplexer_8_out, multiplexer_9_out, multiplexer_10_out, ram_1_data, reg_file_1_a,
       reg_file_1_b, register_1_q, rom_1_data;

  Multiplexer #(.width(32)) multiplexer_1 (
    .in0(multiplexer_3_out), .in1(immediate_generator_1_out_7), .out(multiplexer_1_out),
    .sel(control_unit_1_out_11));  // open: en
  Multiplexer #(.width(32)) multiplexer_2 (
    .in0(multiplexer_1_out), .in1(multiplexer_9_out), .out(multiplexer_2_out), .sel(control_unit_1_out_3));  // open: en
  Clock clock_1 (.out(clock_1_out));
  // Probe on register_1_q_2
  Register #(.width(32)) register_1 (
    .D(multiplexer_2_out), .Q({register_1_q[31:26], register_1_q_2, register_1_q[1:0]}), .clk(clock_1_out),
    .clr(RESET));  // open: en
  Adder #(.width(32)) adder_1 (
    .a(32'h4), .b({register_1_q[31:26], register_1_q_2, register_1_q[1:0]}), .out(adder_1_out));  // open: cin, cout
  Multiplexer #(.width(32)) multiplexer_3 (
    .in0(adder_1_out), .in1(immediate_generator_1_out_5), .out(multiplexer_3_out), .sel(alu_1_out_5));  // open: en
  ROM #(.addrWidth(24), .dataWidth(32)) rom_1 (.addr(register_1_q_2), .data(rom_1_data));  // open: sel
  Immediate_Generator immediate_generator_1 (
    .inst(rom_1_data), .out_3(immediate_generator_1_out_3), .out_4(immediate_generator_1_out_4),
    .out_5(immediate_generator_1_out_5), .out_6(immediate_generator_1_out_6),
    .out_7(immediate_generator_1_out_7), .inst_2({register_1_q[31:26], register_1_q_2, register_1_q[1:0]}));
  CONTROL_UNIT control_unit_1 (
    .in_1(rom_1_data[6:0]), .out_4(control_unit_1_out_4), .out_5(control_unit_1_out_5),
    .out_6(control_unit_1_out_6), .out_7(control_unit_1_out_7), .out_8(control_unit_1_out_8),
    .out_9(control_unit_1_out_9), .out_10(control_unit_1_out_10), .out_3(control_unit_1_out_3),
    .out_11(control_unit_1_out_11), .out_12(control_unit_1_out_12), .out_13(control_unit_1_out_13));  // open: out_2
  Multiplexer #(.width(32)) multiplexer_4 (
    .in0(immediate_generator_1_out_3), .in1(immediate_generator_1_out_4), .out(multiplexer_4_out),
    .sel(control_unit_1_out_7));  // open: en
  // Probe on immediate_generator_1_out_4
  // Probe on undriven_2
  Multiplexer #(.width(5)) multiplexer_5 (
    .in0(rom_1_data[11:7]), .in1(undriven), .out(multiplexer_5_out), .sel(control_unit_1_out_3));  // open: en
  REG_FILE reg_file_1 (
    .EN(control_unit_1_out_6), .rd(multiplexer_5_out), .A(reg_file_1_a), .read_A(rom_1_data[19:15]),
    .B(reg_file_1_b), .read_B(rom_1_data[24:20]), .WRITE_DATA(multiplexer_6_out), .in_6(clock_1_out));
  Multiplexer #(.width(32)) multiplexer_6 (
    .in0(multiplexer_9_out), .in1(multiplexer_10_out), .out(multiplexer_6_out), .sel(control_unit_1_out_3));  // open: en
  Multiplexer #(.select(2), .width(32)) multiplexer_7 (
    .in0(reg_file_1_b), .in1(multiplexer_4_out), .in2(immediate_generator_1_out_6), .out(multiplexer_7_out),
    .sel(control_unit_1_out_10), .en(in_2));  // open: in3
  ALUOP aluop_1 (.FUNC3(rom_1_data[14:12]), .SB(control_unit_1_out_9), .FUNC7(rom_1_data[30]), .out_4(aluop_1_out_4));
  // Probe on undriven_3
  Multiplexer #(.width(32)) multiplexer_8 (
    .in0(reg_file_1_a), .in1(adder_1_out), .out(multiplexer_8_out), .sel(control_unit_1_out_13));  // open: en
  ALU alu_1 (
    .A(multiplexer_8_out), .B(multiplexer_7_out), .out_4(alu_1_out_4), .in_3(aluop_1_out_4),
    .out_5(alu_1_out_5));
  RAM #(.addrWidth(24), .dataWidth(32), .bus("separate")) ram_1 (
    .addr(alu_1_out_4[23:0]), .din(reg_file_1_b), .data(ram_1_data), .str(control_unit_1_out_5), .sel(in_3),
    .clk(clock_1_out), .ld(control_unit_1_out_4));  // open: clr
  Multiplexer #(.width(32)) multiplexer_9 (
    .in0(alu_1_out_4), .in1(ram_1_data), .out(multiplexer_9_out), .sel(control_unit_1_out_8));  // open: en
  Multiplexer #(.width(32)) multiplexer_10 (
    .in0(multiplexer_9_out), .in1(immediate_generator_1_out_6), .out(multiplexer_10_out),
    .sel(control_unit_1_out_12));  // open: en

  // Notes on the sheet:
  //   contents of rom_1 (hex, n*v repeats v):
  //   1100f13 1e02023 693 613 593 100593 2783 60533 168693 b50633 fed780e3 16f713 e0706e3 605b3 fe9ff0ef
  //   OPERAND SEL
endmodule

module ALU (
  input  [31:0] A,
  input  [31:0] B,
  input  [4:0] in_3,
  output [31:0] out_4,
  output out_5
);

  wire and_2_out, comparator_1_lt, comparator_2_eq, comparator_3_lt, comparator_4_eq, comparator_4_gt,
       comparator_5_eq, comparator_6_eq, comparator_7_eq, not_1_out;
  wire [31:0] adder_1_out, and_1_out, bit_extender_1_out, bit_extender_2_out, bit_extender_3_out,
       bit_extender_4_out, bit_extender_5_out, or_1_out, shifter_1_out, shifter_2_out, shifter_3_out,
       subtractor_1_out, xor_1_out;

  assign and_1_out = A & B;  // AND_Gate and_1, 32 bits wide
  assign or_1_out = A | B;  // OR_Gate or_1, 32 bits wide
  Adder #(.width(32)) adder_1 (.a(A), .b(B), .out(adder_1_out));  // open: cin, cout
  Subtractor #(.width(32)) subtractor_1 (.a(A), .b(B), .out(subtractor_1_out));  // open: bin, bout
  Shifter #(.width(32)) shifter_1 (.in(A), .\dist (B[6:2]), .out(shifter_1_out));
  assign xor_1_out = A ^ B;  // XOR_Gate xor_1, 32 bits wide
  Shifter #(.width(32), .shift("lr")) shifter_2 (.in(A), .\dist (B[6:2]), .out(shifter_2_out));
  Shifter #(.width(32), .shift("ar")) shifter_3 (.in(A), .\dist (B[6:2]), .out(shifter_3_out));
  Comparator #(.width(32)) comparator_1 (.a(A), .b(B), .lt(comparator_1_lt));  // open: gt, eq
  Comparator #(.width(32)) comparator_2 (.a(A), .b(B), .eq(comparator_2_eq));  // open: gt, lt
  Comparator #(.width(32)) comparator_3 (.a(A), .b(B), .lt(comparator_3_lt));  // open: gt, eq
  Comparator #(.width(32)) comparator_4 (.a(A), .b(B), .gt(comparator_4_gt), .eq(comparator_4_eq));  // open: lt
  Comparator #(.width(32)) comparator_5 (.a(A), .b(B), .eq(comparator_5_eq));  // open: gt, lt
  assign bit_extender_1_out = {{31{1'b0}}, comparator_1_lt};  // Bit_Extender bit_extender_1
  assign bit_extender_2_out = {{31{1'b0}}, comparator_2_eq};  // Bit_Extender bit_extender_2
  assign bit_extender_3_out = {{31{1'b0}}, comparator_3_lt};  // Bit_Extender bit_extender_3
  and and_2 (and_2_out, comparator_4_gt, comparator_4_eq);
  not not_1 (not_1_out, comparator_5_eq);
  assign bit_extender_4_out = {{31{1'b0}}, and_2_out};  // Bit_Extender bit_extender_4
  assign bit_extender_5_out = {{31{1'b0}}, not_1_out};  // Bit_Extender bit_extender_5
  Multiplexer #(.select(5), .width(32)) multiplexer_1 (
    .in0(adder_1_out), .in1(subtractor_1_out), .in2(bit_extender_2_out), .in4(shifter_1_out),
    .in6(bit_extender_5_out), .in8(bit_extender_1_out), .in16(xor_1_out), .in18(bit_extender_3_out),
    .in20(shifter_2_out), .in21(shifter_3_out), .in22(bit_extender_4_out), .in24(or_1_out), .in28(and_1_out),
    .out(out_4), .sel(in_3));  // open: in3, in5, in7, in9, in10, in11, in12, in13, in14, in15, in17, in19, in23, in25, in26, in27, in29, in30, in31, en
  Comparator #(.width(2)) comparator_6 (.a({in_3[2], in_3[0]}), .b(2'b10), .eq(comparator_6_eq));  // open: gt, lt
  Comparator #(.width(32)) comparator_7 (.a(out_4), .b(32'h1), .eq(comparator_7_eq));  // open: gt, lt
  // Probe on out_4
  and and_3 (out_5, comparator_6_eq, comparator_7_eq);
endmodule

module REG_FILE (
  input  [31:0] WRITE_DATA,
  input  EN,
  input  [4:0] read_A,
  input  [4:0] rd,
  input  [4:0] read_B,
  input  in_6,
  output [31:0] A,
  output [31:0] B
);

  wire demultiplexer_1_out0, demultiplexer_1_out1, demultiplexer_1_out2, demultiplexer_1_out3,
       demultiplexer_1_out4, demultiplexer_1_out5, demultiplexer_1_out6, demultiplexer_1_out7,
       demultiplexer_1_out8, demultiplexer_1_out9, demultiplexer_1_out10, demultiplexer_1_out11,
       demultiplexer_1_out12, demultiplexer_1_out13, demultiplexer_1_out14, demultiplexer_1_out15,
       demultiplexer_1_out16, demultiplexer_1_out17, demultiplexer_1_out18, demultiplexer_1_out19,
       demultiplexer_1_out20, demultiplexer_1_out21, demultiplexer_1_out22, demultiplexer_1_out23,
       demultiplexer_1_out24, demultiplexer_1_out25, demultiplexer_1_out26, demultiplexer_1_out27,
       demultiplexer_1_out28, demultiplexer_1_out29, demultiplexer_1_out30, demultiplexer_1_out31;
  wire [31:0] register_1_q, register_2_q, register_3_q, register_4_q, register_5_q, register_6_q,
       register_7_q, register_8_q, register_9_q, register_10_q, register_11_q, register_12_q, register_13_q,
       register_14_q, register_15_q, register_16_q, register_17_q, register_18_q, register_19_q,
       register_20_q, register_21_q, register_22_q, register_23_q, register_24_q, register_25_q,
       register_26_q, register_27_q, register_28_q, register_29_q, register_30_q, register_31_q,
       register_32_q;

  Demultiplexer #(.select(5)) demultiplexer_1 (
    .out0(demultiplexer_1_out0), .out1(demultiplexer_1_out1), .out2(demultiplexer_1_out2),
    .out3(demultiplexer_1_out3), .out4(demultiplexer_1_out4), .out5(demultiplexer_1_out5),
    .out6(demultiplexer_1_out6), .out7(demultiplexer_1_out7), .out8(demultiplexer_1_out8),
    .out9(demultiplexer_1_out9), .out10(demultiplexer_1_out10), .out11(demultiplexer_1_out11),
    .out12(demultiplexer_1_out12), .out13(demultiplexer_1_out13), .out14(demultiplexer_1_out14),
    .out15(demultiplexer_1_out15), .out16(demultiplexer_1_out16), .out17(demultiplexer_1_out17),
    .out18(demultiplexer_1_out18), .out19(demultiplexer_1_out19), .out20(demultiplexer_1_out20),
    .out21(demultiplexer_1_out21), .out22(demultiplexer_1_out22), .out23(demultiplexer_1_out23),
    .out24(demultiplexer_1_out24), .out25(demultiplexer_1_out25), .out26(demultiplexer_1_out26),
    .out27(demultiplexer_1_out27), .out28(demultiplexer_1_out28), .out29(demultiplexer_1_out29),
    .out30(demultiplexer_1_out30), .out31(demultiplexer_1_out31), .in(EN), .sel(rd));  // open: en
  Register #(.width(32)) register_1 (
    .D({32{1'b0}}), .en(demultiplexer_1_out0), .Q(register_1_q), .clk(in_6));  // open: clr
  Register #(.width(32)) register_2 (
    .D(WRITE_DATA), .en(demultiplexer_1_out1), .Q(register_2_q), .clk(in_6));  // open: clr
  Register #(.width(32)) register_3 (
    .D(WRITE_DATA), .en(demultiplexer_1_out2), .Q(register_3_q), .clk(in_6));  // open: clr
  Register #(.width(32)) register_4 (
    .D(WRITE_DATA), .en(demultiplexer_1_out3), .Q(register_4_q), .clk(in_6));  // open: clr
  Register #(.width(32)) register_5 (
    .D(WRITE_DATA), .en(demultiplexer_1_out4), .Q(register_5_q), .clk(in_6));  // open: clr
  Register #(.width(32)) register_6 (
    .D(WRITE_DATA), .en(demultiplexer_1_out5), .Q(register_6_q), .clk(in_6));  // open: clr
  Register #(.width(32)) register_7 (
    .D(WRITE_DATA), .en(demultiplexer_1_out6), .Q(register_7_q), .clk(in_6));  // open: clr
  Register #(.width(32)) register_8 (
    .D(WRITE_DATA), .en(demultiplexer_1_out7), .Q(register_8_q), .clk(in_6));  // open: clr
  Register #(.width(32)) register_9 (
    .D(WRITE_DATA), .en(demultiplexer_1_out8), .Q(register_9_q), .clk(in_6));  // open: clr
  Register #(.width(32)) register_10 (
    .D(WRITE_DATA), .en(demultiplexer_1_out9), .Q(register_10_q), .clk(in_6));  // open: clr
  Register #(.width(32)) register_11 (
    .D(WRITE_DATA), .en(demultiplexer_1_out10), .Q(register_11_q), .clk(in_6));  // open: clr
  Register #(.width(32)) register_12 (
    .D(WRITE_DATA), .en(demultiplexer_1_out11), .Q(register_12_q), .clk(in_6));  // open: clr
  Register #(.width(32)) register_13 (
    .D(WRITE_DATA), .en(demultiplexer_1_out12), .Q(register_13_q), .clk(in_6));  // open: clr
  Register #(.width(32)) register_14 (
    .D(WRITE_DATA), .en(demultiplexer_1_out13), .Q(register_14_q), .clk(in_6));  // open: clr
  Register #(.width(32)) register_15 (
    .D(WRITE_DATA), .en(demultiplexer_1_out14), .Q(register_15_q), .clk(in_6));  // open: clr
  Register #(.width(32)) register_16 (
    .D(WRITE_DATA), .en(demultiplexer_1_out15), .Q(register_16_q), .clk(in_6));  // open: clr
  Register #(.width(32)) register_17 (
    .D(WRITE_DATA), .en(demultiplexer_1_out16), .Q(register_17_q), .clk(in_6));  // open: clr
  Register #(.width(32)) register_18 (
    .D(WRITE_DATA), .en(demultiplexer_1_out17), .Q(register_18_q), .clk(in_6));  // open: clr
  Register #(.width(32)) register_19 (
    .D(WRITE_DATA), .en(demultiplexer_1_out18), .Q(register_19_q), .clk(in_6));  // open: clr
  Register #(.width(32)) register_20 (
    .D(WRITE_DATA), .en(demultiplexer_1_out19), .Q(register_20_q), .clk(in_6));  // open: clr
  Register #(.width(32)) register_21 (
    .D(WRITE_DATA), .en(demultiplexer_1_out20), .Q(register_21_q), .clk(in_6));  // open: clr
  Register #(.width(32)) register_22 (
    .D(WRITE_DATA), .en(demultiplexer_1_out21), .Q(register_22_q), .clk(in_6));  // open: clr
  Register #(.width(32)) register_23 (
    .D(WRITE_DATA), .en(demultiplexer_1_out22), .Q(register_23_q), .clk(in_6));  // open: clr
  Register #(.width(32)) register_24 (
    .D(WRITE_DATA), .en(demultiplexer_1_out23), .Q(register_24_q), .clk(in_6));  // open: clr
  Register #(.width(32)) register_25 (
    .D(WRITE_DATA), .en(demultiplexer_1_out24), .Q(register_25_q), .clk(in_6));  // open: clr
  Register #(.width(32)) register_26 (
    .D(WRITE_DATA), .en(demultiplexer_1_out25), .Q(register_26_q), .clk(in_6));  // open: clr
  Register #(.width(32)) register_27 (
    .D(WRITE_DATA), .en(demultiplexer_1_out26), .Q(register_27_q), .clk(in_6));  // open: clr
  Register #(.width(32)) register_28 (
    .D(WRITE_DATA), .en(demultiplexer_1_out27), .Q(register_28_q), .clk(in_6));  // open: clr
  Register #(.width(32)) register_29 (
    .D(WRITE_DATA), .en(demultiplexer_1_out28), .Q(register_29_q), .clk(in_6));  // open: clr
  Register #(.width(32)) register_30 (
    .D(WRITE_DATA), .en(demultiplexer_1_out29), .Q(register_30_q), .clk(in_6));  // open: clr
  Register #(.width(32)) register_31 (
    .D(WRITE_DATA), .en(demultiplexer_1_out30), .Q(register_31_q), .clk(in_6));  // open: clr
  Register #(.width(32)) register_32 (
    .D(WRITE_DATA), .en(demultiplexer_1_out31), .Q(register_32_q), .clk(in_6));  // open: clr
  Multiplexer #(.select(5), .width(32)) multiplexer_1 (
    .in0(register_1_q), .in1(register_2_q), .in2(register_3_q), .in3(register_4_q), .in4(register_5_q),
    .in5(register_6_q), .in6(register_7_q), .in7(register_8_q), .in8(register_9_q), .in9(register_10_q),
    .in10(register_11_q), .in11(register_12_q), .in12(register_13_q), .in13(register_14_q),
    .in14(register_15_q), .in15(register_16_q), .in16(register_17_q), .in17(register_18_q),
    .in18(register_19_q), .in19(register_20_q), .in20(register_21_q), .in21(register_22_q),
    .in22(register_23_q), .in23(register_24_q), .in24(register_25_q), .in25(register_26_q),
    .in26(register_27_q), .in27(register_28_q), .in28(register_29_q), .in29(register_30_q),
    .in30(register_31_q), .in31(register_32_q), .out(A), .sel(read_A));  // open: en
  Multiplexer #(.select(5), .width(32)) multiplexer_2 (
    .in0(register_1_q), .in1(register_2_q), .in2(register_3_q), .in3(register_4_q), .in4(register_5_q),
    .in5(register_6_q), .in6(register_7_q), .in7(register_8_q), .in8(register_9_q), .in9(register_10_q),
    .in10(register_11_q), .in11(register_12_q), .in12(register_13_q), .in13(register_14_q),
    .in14(register_15_q), .in15(register_16_q), .in16(register_17_q), .in17(register_18_q),
    .in18(register_19_q), .in19(register_20_q), .in20(register_21_q), .in21(register_22_q),
    .in22(register_23_q), .in23(register_24_q), .in24(register_25_q), .in25(register_26_q),
    .in26(register_27_q), .in27(register_28_q), .in28(register_29_q), .in29(register_30_q),
    .in30(register_31_q), .in31(register_32_q), .out(B), .sel(read_B));  // open: en
endmodule

module Immediate_Generator (
  input  [31:0] inst,
  input  [31:0] inst_2,
  output [31:0] out_3,
  output [31:0] out_4,
  output [31:0] out_5,
  output [31:0] out_6,
  output [31:0] out_7
);

  wire undriven_3;
  wire [0:0] undriven, undriven_2;
  wire [31:0] bit_extender_4_out, bit_extender_5_out, shifter_1_out, shifter_2_out;

  assign out_3 = {{20{inst[31]}}, inst[31:20]};  // Bit_Extender bit_extender_1
  assign out_6 = {{12{inst[31]}}, inst[31:12]};  // Bit_Extender bit_extender_2
  assign out_4 = {{20{inst[31]}}, {inst[31:25], inst[11:7]}};  // Bit_Extender bit_extender_3
  assign bit_extender_4_out = {{11{inst[31]}}, {inst[31], inst[19:12], inst[20], inst[30:21], undriven[0]}};  // Bit_Extender bit_extender_4
  assign bit_extender_5_out = {{19{inst[31]}}, {inst[31], inst[7], inst[30:25], inst[11:8], undriven_2[0]}};  // Bit_Extender bit_extender_5
  // Probe on undriven_3
  Shifter #(.width(32), .shift("lr")) shifter_1 (.in(bit_extender_4_out), .\dist (5'b00001), .out(shifter_1_out));
  Shifter #(.width(32), .shift("lr")) shifter_2 (.in(bit_extender_5_out), .\dist (5'b00001), .out(shifter_2_out));
  // Probe on out_3
  Adder #(.width(32)) adder_1 (.a(shifter_2_out), .b(inst_2), .out(out_5));  // open: cin, cout
  Adder #(.width(32)) adder_2 (.a(shifter_1_out), .b(inst_2), .out(out_7));  // open: cin, cout

  // Notes on the sheet:
  //   0-11
  //   I-TYPE
  //   S-TYPE
  //   SB-TYPE
  //   U - TYPE
  //   UJ - TYPE
  //   7-11 = 5 , 25 - 31 = 7 , 12 BIT KE SPLITER SE HUM 7-11 KO 0-4 PR RAKHEIN GYE AND 25-11 , 5-11 , BIT EXTENDER IS LEI NAHI LAGYA KYUN KE HUMEIN 12 BIT PR INKO MAP KARNA THA
endmodule

module OP_CODE (
  input  [6:0] OPCODE,
  output R_TYPE,
  output LOAD,
  output I___TYPE,
  output S___TYPE,
  output SB___TYPE,
  output LUI,
  output JAL,
  output JALR,
  output out_10
);

  Comparator #(.width(7)) comparator_1 (.a(7'b0110011), .b(OPCODE), .eq(R_TYPE));  // open: gt, lt
  Comparator #(.width(7)) comparator_2 (.a(7'b0000011), .b(OPCODE), .eq(LOAD));  // open: gt, lt
  Comparator #(.width(7)) comparator_3 (.a(7'b0010011), .b(OPCODE), .eq(I___TYPE));  // open: gt, lt
  Comparator #(.width(7)) comparator_4 (.a(7'b0100011), .b(OPCODE), .eq(S___TYPE));  // open: gt, lt
  Comparator #(.width(7)) comparator_5 (.a(7'b1100011), .b(OPCODE), .eq(SB___TYPE));  // open: gt, lt
  Comparator #(.width(7)) comparator_6 (.a(7'b0110111), .b(OPCODE), .eq(LUI));  // open: gt, lt
  Comparator #(.width(7)) comparator_7 (.a(7'b1101111), .b(OPCODE), .eq(JAL));  // open: gt, lt
  Comparator #(.width(7)) comparator_8 (.a(7'b1100111), .b(OPCODE), .eq(JALR));  // open: gt, lt
  Comparator #(.width(7)) comparator_9 (.a(7'b0010111), .b(OPCODE), .eq(out_10));  // open: gt, lt
endmodule

module controller (
  input  R_TYPE,
  input  I_TYPE,
  input  LOAD,
  input  STORE,
  input  LUI,
  input  JAL,
  input  JALR,
  input  SB,
  input  AUIPC,
  output MEMREAD,
  output MEMWRITE,
  output REGWRITE,
  output LUI_2,
  output IMMSEL,
  output LOAD_SEL,
  output BRANCH,
  output [1:0] operand_sel,
  output JAL_2,
  output JALR_2,
  output LUI_3,
  output AUIPC_2
);

  or or_1 (REGWRITE, R_TYPE, I_TYPE, LOAD, STORE, LUI, JAL, JALR);
  or or_2 (operand_sel[0], I_TYPE, STORE, JALR);

  assign AUIPC_2 = AUIPC;
  assign BRANCH = SB;
  assign IMMSEL = STORE;
  assign JAL_2 = JAL;
  assign JALR_2 = JALR;
  assign LOAD_SEL = LOAD;
  assign LUI_2 = LUI;
  assign LUI_3 = LUI;
  assign MEMREAD = LOAD;
  assign MEMWRITE = STORE;
  assign operand_sel[1] = AUIPC;
endmodule

module CONTROL_UNIT (
  input  [6:0] in_1,
  output out_2,
  output out_3,
  output out_4,
  output out_5,
  output out_6,
  output out_7,
  output out_8,
  output out_9,
  output [1:0] out_10,
  output out_11,
  output out_12,
  output out_13
);

  wire op_code_1_i___type, op_code_1_jal, op_code_1_jalr, op_code_1_load, op_code_1_lui, op_code_1_out_10,
       op_code_1_r_type, op_code_1_s___type, op_code_1_sb___type;

  OP_CODE op_code_1 (
    .OPCODE(in_1), .LOAD(op_code_1_load), .I___TYPE(op_code_1_i___type), .S___TYPE(op_code_1_s___type),
    .SB___TYPE(op_code_1_sb___type), .LUI(op_code_1_lui), .JAL(op_code_1_jal), .JALR(op_code_1_jalr),
    .R_TYPE(op_code_1_r_type), .out_10(op_code_1_out_10));
  controller controller_1 (
    .MEMREAD(out_4), .MEMWRITE(out_5), .REGWRITE(out_6), .IMMSEL(out_7), .LOAD_SEL(out_8), .BRANCH(out_9),
    .R_TYPE(op_code_1_r_type), .I_TYPE(op_code_1_i___type), .LOAD(op_code_1_load),
    .STORE(op_code_1_s___type), .LUI(op_code_1_lui), .JAL(op_code_1_jal), .JALR(op_code_1_jalr),
    .SB(op_code_1_sb___type), .operand_sel(out_10), .JAL_2(out_11), .JALR_2(out_3), .LUI_2(out_13),
    .LUI_3(out_12), .AUIPC(op_code_1_out_10), .AUIPC_2(out_2));

  // Notes on the sheet:
  //   OPERAND SEL
endmodule

module ALUOP (
  input  [2:0] FUNC3,
  input  SB,
  input  FUNC7,
  output [4:0] out_4
);


  assign out_4 = {FUNC3, SB, FUNC7};
endmodule
